# Fritzing sketch ThreeSwitches (saved by Fritzing 0.9.10b)
circuit board: 6.67286cm x 5.19451cm
breadboards: 1

parts:
  Nano = Arduino Nano (Rev3.0)
  +5v- = Screw terminal - 2 pins [package=THT]
  R4 = Resistor [tolerance=±5% power=0.25 resistance=1k package=THT]
  R5 = Resistor [tolerance=±5% power=0.25 resistance=1k package=THT]
  R6 = Resistor [tolerance=±5% power=0.25 resistance=1k package=THT]
  Q1 = NPN-Transistor [package="TO92 [THT]"]
  RY1 = HF41F relay
  R2 = Resistor [tolerance=±5% power=0.25 resistance=1k package=THT]
  D1 = Rectifier Diode [part_number=1N4001 package="300 mil [THT]"]
  R7 = Resistor [tolerance=±5% power=0.25 resistance=1k package=THT]
  Q2 = NPN-Transistor [package="TO92 [THT]"]
  RY2 = HF41F relay
  D2 = Rectifier Diode [part_number=1N4001 package="300 mil [THT]"]
  R8 = Resistor [tolerance=±5% power=0.25 resistance=1k package=THT]
  Q3 = NPN-Transistor [package="TO92 [THT]"]
  RY3 = HF41F relay
  D3 = Rectifier Diode [part_number=1N4001 package="300 mil [THT]"]
  ser_3 = Dagu DGServo 9g header (male) [package=THT]
  ser_2 = Dagu DGServo 9g header (male) [package=THT]
  ser_1 = Dagu DGServo 9g header (male) [package=THT]
  sw3 = Dagu DGServo 9g header (male) [package=THT]
  sw2 = Dagu DGServo 9g header (male) [package=THT]
  sw1 = Dagu DGServo 9g header (male) [package=THT]
  1_2_3 = Dagu DGServo 9g header (male) [package=THT]

nets:
  GND: Nano.GND, +5v-.pin1, R4.Pin_1, R5.Pin_1, R6.Pin_1, Q1.E, Q2.E, Q3.E, ser_3.gnd, ser_2.gnd, ser_1.gnd
  N1: Nano.D2, ser_1.pulse
  N2: Nano.D3, R2.Pin_1
  N3: Nano.D4, R4.Pin_0, 1_2_3.gnd
  N4: Nano.D5, ser_2.pulse
  N5: Nano.D6, R7.Pin_1
  N6: Nano.D7, R5.Pin_0, 1_2_3.Vcc
  N7: Nano.D8, ser_3.pulse
  N8: Nano.D9, R8.Pin_1
  N9: Nano.D10, R6.Pin_0, 1_2_3.pulse
  VCC: Nano.VIN, +5v-.pin2, RY1.Pin_1, D1.cathode, RY2.Pin_1, D2.cathode, RY3.Pin_1, D3.cathode, ser_3.Vcc, ser_2.Vcc, ser_1.Vcc
  N10: Q1.B, R2.Pin_0
  N11: Q1.C, RY1.Pin_2, D1.anode
  N12: RY1.Pin_3, sw1.gnd
  N13: RY1.Pin_4, sw1.Vcc
  N14: RY1.Pin_5, sw1.pulse
  N15: R7.Pin_0, Q2.B
  N16: Q2.C, RY2.Pin_2, D2.anode
  N17: RY2.Pin_3, sw2.gnd
  N18: RY2.Pin_4, sw2.Vcc
  N19: RY2.Pin_5, sw2.pulse
  N20: R8.Pin_0, Q3.B
  N21: Q3.C, RY3.Pin_2, D3.anode
  N22: RY3.Pin_3, sw3.gnd
  N23: RY3.Pin_4, sw3.Vcc
  N24: RY3.Pin_5, sw3.pulse

custom parts:
  HF41F relay: Subminiature Power Relay 1 form C.
