# Fritzing sketch TwoShortBridge (saved by Fritzing 0.9.10b)
circuit board: 11.1549cm x 6.36194cm
breadboards: 2

parts:
  Nano = Arduino Nano (Rev3.0) (ICSP)
  Bridge1 = screw terminal, 4 pins
  Bridge2 = screw terminal, 4 pins
  Sens1l = screw terminal, 3 pins
  Sens2l = screw terminal, 3 pins
  Sens1R = screw terminal, 3 pins
  Sens2r = screw terminal, 3 pins
  DFPlayer_Mini1 = DFRobot DFPlayer Mini [part_number=DFR0299]
  OLEDs = screw terminal, 4 pins
  -5V+ = Screw terminal - 2 pins [package=THT]
  Q1 = PNP-Transistor [package="TO92 [THT]"]
  Q2 = PNP-Transistor [package="TO92 [THT]"]
  Q3 = PNP-Transistor [package="TO92 [THT]"]
  Q4 = PNP-Transistor [package="TO92 [THT]"]
  Q5 = PNP-Transistor [package="TO92 [THT]"]
  Q6 = PNP-Transistor [package="TO92 [THT]"]
  AMP1 = PAM8403 6W Stereo Amplifier
  Loud1 = Screw terminal - 2 pins [package=THT]
  Loud2 = Screw terminal - 2 pins [package=THT]
  R1 = Resistor [tolerance=±5% power=0.25 resistance=1000 package=THT]
  R2 = Resistor [tolerance=±5% power=0.25 resistance=1000 package=THT]
  R3 = Resistor [tolerance=±5% power=0.25 resistance=1000 package=THT]
  R4 = Resistor [tolerance=±5% power=0.25 resistance=1000 package=THT]
  R5 = Resistor [tolerance=±5% power=0.25 resistance=1000 package=THT]
  R6 = Resistor [tolerance=±5% power=0.25 resistance=1000 package=THT]
  R7 = Resistor [tolerance=±5% power=0.25 resistance=1000 package=THT]
  R8 = Resistor [tolerance=±5% power=0.25 resistance=1000 package=THT]

nets:
  N1: Nano.GND, Bridge1.pin1, Bridge2.pin1, Sens1l.pin1, Sens2l.pin1, Sens1R.pin1, Sens2r.pin1, DFPlayer_Mini1.GND-1, DFPlayer_Mini1.GND-2, OLEDs.pin1, -5V+.pin1, AMP1.Ground
  N2: Nano.D2, R2.Pin_1
  N3: Nano.D3, R3.Pin_1
  N4: Nano.D4, Sens1R.pin3
  N5: Nano.D5, Sens1l.pin3
  N6: Nano.D6, R7.Pin_1
  N7: Nano.D7, R8.Pin_1
  N8: Nano.D8, R4.Pin_1
  N9: Nano.D9, R1.Pin_1
  N10: Nano.D10, R5.Pin_1
  N11: Nano.D11/MOSI, R6.Pin_1
  N12: Nano.D12/MISO, Sens2r.pin3
  VIN: Nano.VIN, Sens1l.pin2, Sens2l.pin2, Sens1R.pin2, Sens2r.pin2, DFPlayer_Mini1.VCC, OLEDs.pin2, -5V+.pin2, Q1.E, Q2.E, Q3.E, Q4.E, Q5.E, Q6.E, AMP1.5V
  N13: Nano.A5, OLEDs.pin4
  N14: Nano.A4, OLEDs.pin3
  N15: Nano.A2, Sens2l.pin3
  N16: Bridge1.pin2, Q1.C
  N17: Bridge1.pin3, Q2.C
  N18: Bridge1.pin4, Q3.C
  N19: Bridge2.pin2, Q4.C
  N20: Bridge2.pin3, Q5.C
  N21: Bridge2.pin4, Q6.C
  N22: DFPlayer_Mini1.RX, R8.Pin_0
  N23: DFPlayer_Mini1.TX, R7.Pin_0
  N24: DFPlayer_Mini1.SPK_1, AMP1.R_Input
  N25: DFPlayer_Mini1.SPK_2, AMP1.L_Input
  N26: Q1.B, R2.Pin_0
  N27: Q2.B, R1.Pin_0
  N28: Q3.B, R3.Pin_0
  N29: Q4.B, R4.Pin_0
  N30: Q5.B, R5.Pin_0
  N31: Q6.B, R6.Pin_0
  N32: AMP1.L_Out_-, Loud1.pin1
  N33: AMP1.L_Out_+, Loud1.pin2
  N34: AMP1.R_Out_-, Loud2.pin2
  N35: AMP1.R_Out_+, Loud2.pin1

notes:
  TwoShortBrdige fca 2025

custom parts:
  PAM8403 6W Stereo Amplifier: PAM8403 6 Watt Stereo Amplifier
